# Fritzing sketch conector fpga (saved by Fritzing 0.9.4)
circuit board: 4.67702cm x 4.03746cm
breadboards: 1

parts:
  VGA_FEMALE1 = DB15 VGA Connector [package=db15]
  R1 = Resistor [tolerance=±5% resistance=270 package=THT]
  R2 = Resistor [tolerance=±5% resistance=560 package=THT]
  R3 = Resistor [tolerance=±5% resistance=1M package=THT]
  R4 = Resistor [tolerance=±5% resistance=1M package=THT]
  R5 = Resistor [tolerance=±5% resistance=270 package=THT]
  R6 = Resistor [tolerance=±5% resistance=1M package=THT]
  R7 = Resistor [tolerance=±5% resistance=270 package=THT]
  R8 = Resistor [tolerance=±5% resistance=560 package=THT]
  R9 = Resistor [tolerance=±5% resistance=270 package=THT]
  J1 = female pin header, 12 pins [form="♀ (female)"]
  R10 = Resistor [tolerance=±5% resistance=100 package=THT]
  R11 = Resistor [tolerance=±5% resistance=100 package=THT]
  R12 = Resistor [tolerance=±5% resistance=150 package=THT]
  R13 = Resistor [tolerance=±5% resistance=150 package=THT]
  R14 = Resistor [tolerance=±5% resistance=150 package=THT]

nets:
  N1: VGA_FEMALE1.1, R7.Pin_1, R8.Pin_1, R9.Pin_1, R14.Pin_0
  N2: VGA_FEMALE1.2, R4.Pin_1, R5.Pin_1, R6.Pin_1, R13.Pin_0
  N3: VGA_FEMALE1.3, R1.Pin_1, R2.Pin_1, R3.Pin_1, R12.Pin_0
  GND: VGA_FEMALE1.5, VGA_FEMALE1.6, VGA_FEMALE1.7, VGA_FEMALE1.8, VGA_FEMALE1.pin_10, J1.pin12, R12.Pin_1, R13.Pin_1, R14.Pin_1
  N4: VGA_FEMALE1.pin_14, R10.Pin_1
  N5: VGA_FEMALE1.pin_15, R11.Pin_1
  N6: R1.Pin_0, J1.pin1
  N7: R2.Pin_0, J1.pin2
  N8: R3.Pin_0, J1.pin3
  N9: R4.Pin_0, J1.pin4
  N10: R5.Pin_0, J1.pin5
  N11: R6.Pin_0, J1.pin6
  N12: R7.Pin_0, J1.pin7
  N13: R8.Pin_0, J1.pin8
  N14: R9.Pin_0, J1.pin9
  N15: J1.pin10, R10.Pin_0
  N16: J1.pin11, R11.Pin_0

notes:
  FPGA-VGA 0.0.2
